# Fritzing sketch ArduinoAQI_mini (saved by Fritzing 0.9.4)

parts:
  Grove1 = Grove 4 Digit Display
  WiFi_Reset = Pushbutton [package="[THT]"]
  PMS5003 = double row female pin header, 8 pins [form="♀ (female)"]
  WeMos_D1_Mini1 = WeMos D1 Mini

nets:
  N1: Grove1.GND, WiFi_Reset.Pin_1, WiFi_Reset.Pin_2, PMS5003.pin2, WeMos_D1_Mini1.G
  VCC: Grove1.VCC, PMS5003.pin1, WeMos_D1_Mini1.5V
  N2: Grove1.DIO, WeMos_D1_Mini1.D6
  N3: Grove1.CLK, WeMos_D1_Mini1.D5
  N4: WiFi_Reset.Pin_3, WiFi_Reset.Pin_4, WeMos_D1_Mini1.D7
  N5: PMS5003.pin4, WeMos_D1_Mini1.D2
  N6: PMS5003.pin5, WeMos_D1_Mini1.D1
